// Logisim project GCore.circ as structural Verilog: 9 circuits, main circuit main
module main (
);

  wire alu_zero, and_1_out, clk_out, clock_accclk, clock_aluclk, clock_clkout, clock_memclk, clock_opramclk,
       clock_pcclk, control_accwrite, control_branch, control_jump, control_memread, control_memwrite,
       multiplexer_1_out, or_1_out;
  wire [1:0] control_accdst;
  wire [2:0] control_aluop;
  wire [7:0] alu_ans, bit_extender_1_out, mem_control_data, multiplexer_2_out, mux_out, opram_control_op,
       pc_addr, shifter_1_out, undriven;

  Clock clk (.out(clk_out));
  clock clock (
    .clock(clk_out), .pcclk(clock_pcclk), .opramclk(clock_opramclk), .memclk(clock_memclk),
    .aluclk(clock_aluclk), .accclk(clock_accclk), .clkout(clock_clkout));
  pc pc (.jumpaddr(mem_control_data), .jump(or_1_out), .clk(1'b0), .rst(clock_pcclk), .addr(pc_addr));
  Multiplexer #(.enable("false")) multiplexer_1 (.in0(clock_opramclk), .in1(1'b0), .out(multiplexer_1_out), .sel(1'b0));
  or or_1 (or_1_out, and_1_out, control_jump);
  Multiplexer #(.width(8), .enable("false")) multiplexer_2 (
    .in0(pc_addr), .in1({8{1'b0}}), .out(multiplexer_2_out), .sel(1'b0));
  opram_control opram_control (
    .addr(multiplexer_2_out), .writeop({8{1'b0}}), .write(1'b0), .read(1'b1), .clk(multiplexer_1_out),
    .rst(1'b0), .op(opram_control_op));
  and and_1 (and_1_out, alu_zero, control_branch);
  control control (
    .op(opram_control_op[7:4]), .aluop(control_aluop), .accdst(control_accdst), .jump(control_jump),
    .branch(control_branch), .accwrite(control_accwrite), .memread(control_memread),
    .memwrite(control_memwrite));
  mem_control mem_control (
    .addr(opram_control_op[3:0]), .writedata(undriven), .write(control_memwrite), .read(control_memread),
    .clk(clock_memclk), .rst(1'b0), .data(mem_control_data));
  assign bit_extender_1_out = {{4{1'b0}}, opram_control_op[3:0]};  // Bit_Extender bit_extender_1
  mux mux (
    .a(mem_control_data), .b(bit_extender_1_out), .c(alu_ans), .d(shifter_1_out), .sel(control_accdst),
    .out(mux_out));
  accum accum (.writedata(mux_out), .write(control_accwrite), .clk(clock_accclk), .rst(1'b0), .data(undriven));
  alu alu (
    .b(mem_control_data), .a(undriven), .aluop(control_aluop), .clk(clock_aluclk), .zero(alu_zero),
    .ans(alu_ans));
  Shifter shifter_1 (.in(undriven), .\dist (3'b100), .out(shifter_1_out));
  LED led_1 (.in(undriven[0]));
  LED led_2 (.in(undriven[1]));
  LED led_3 (.in(undriven[2]));
  LED led_4 (.in(undriven[3]));
  LED led_5 (.in(undriven[4]));
  LED led_6 (.in(undriven[5]));
  LED led_7 (.in(undriven[6]));
  LED led_8 (.in(undriven[7]));
  LED led_9 (.in(clock_clkout));

  // Notes on the sheet:
  //   writeclk
  //   opwrite
  //   opread
  //   writeaddr
  //   writeop
  //   rst
  //   acc out
  //   clk out
endmodule

module pc (
  input  [7:0] jumpaddr,
  input  jump,
  input  clk,
  input  rst,
  output [7:0] addr
);

  wire [7:0] adder_1_out, multiplexer_1_out;

  Adder adder_1 (.a(addr), .b(8'h1), .out(adder_1_out));  // open: cin, cout
  Multiplexer #(.width(8), .enable("false")) multiplexer_1 (
    .in0(adder_1_out), .in1(jumpaddr), .out(multiplexer_1_out), .sel(jump));
  Register Mem (.D(multiplexer_1_out), .en(1'b1), .Q(addr), .clk(clk), .clr(rst));
endmodule

module mem_control (
  input  [3:0] addr,
  input  [7:0] writedata,
  input  write,
  input  read,
  input  clk,
  input  rst,
  output [7:0] data
);

  RAM #(.addrWidth(4), .bus("separate")) ram_1 (
    .addr(addr), .din(writedata), .data(data), .str(write), .sel(1'b1), .clk(clk), .ld(read), .clr(rst));
endmodule

module opram_control (
  input  [7:0] addr,
  input  [7:0] writeop,
  input  write,
  input  read,
  input  clk,
  input  rst,
  output [7:0] op
);

  wire and_1_out, not_1_out;

  not not_1 (not_1_out, write);
  and and_1 (and_1_out, not_1_out, read);
  RAM #(.bus("separate")) ram_1 (
    .addr(addr), .din(writeop), .data(op), .str(write), .sel(1'b1), .clk(clk), .ld(and_1_out), .clr(rst));
endmodule

module mux (
  input  [7:0] a,
  input  [7:0] b,
  input  [7:0] c,
  input  [7:0] d,
  input  [1:0] sel,
  output [7:0] out
);

  Multiplexer #(.select(2), .width(8), .enable("false")) multiplexer_1 (
    .in0(a), .in1(b), .in2(c), .in3(d), .out(out), .sel(sel));
endmodule

module accum (
  input  [7:0] writedata,
  input  [7:0] data,
  input  write,
  input  clk,
  input  rst
);

  wire [7:0] Mem_q, multiplexer_1_out, multiplexer_2_out;

  Multiplexer #(.width(8), .enable("false")) multiplexer_1 (
    .in0(Mem_q), .in1(writedata), .out(multiplexer_1_out), .sel(write));
  Multiplexer #(.width(8), .enable("false")) multiplexer_2 (
    .in0(multiplexer_1_out), .in1({8{1'b0}}), .out(multiplexer_2_out), .sel(rst));
  Register Mem (.D(multiplexer_2_out), .en(1'b1), .Q(Mem_q), .clk(clk), .clr(1'b0));
  assign data = Mem_q;  // Buffer buffer_1, 8 bits wide
endmodule

module alu (
  input  [7:0] b,
  input  [7:0] a,
  input  [2:0] aluop,
  input  clk,
  output zero,
  output [7:0] ans
);

  wire [0:0] comparator_1_lt, comparator_2_eq;
  wire [7:0] adder_1_out, and_1_out, multiplexer_1_out, or_1_out, subtractor_1_out, xor_1_out;

  Adder adder_1 (.a(a), .b(b), .out(adder_1_out));  // open: cin, cout
  Subtractor subtractor_1 (.a(a), .b(b), .out(subtractor_1_out));  // open: bin, bout
  assign and_1_out = a & b;  // AND_Gate and_1, 8 bits wide
  assign or_1_out = a | b;  // OR_Gate or_1, 8 bits wide
  assign xor_1_out = a ^ b;  // XOR_Gate xor_1, 8 bits wide
  Comparator comparator_1 (.a(a), .b(b), .lt(comparator_1_lt[0]));  // open: gt, eq
  Comparator comparator_2 (.a(a), .b(b), .eq(comparator_2_eq[0]));  // open: gt, lt
  Multiplexer #(.select(3), .width(8), .enable("false")) multiplexer_1 (
    .in0(adder_1_out), .in1(subtractor_1_out), .in2(and_1_out), .in3(or_1_out), .in4(xor_1_out),
    .in5({8{1'b0}}), .in6({{7{1'b0}}, comparator_1_lt[0]}), .in7({{7{1'b0}}, comparator_2_eq[0]}),
    .out(multiplexer_1_out), .sel(aluop));
  Register Mem (.D(multiplexer_1_out), .en(1'b1), .Q(ans), .clk(clk), .clr(1'b0));

  assign zero = ans[0];
endmodule

module control (
  input  [3:0] op,
  output [2:0] aluop,
  output [1:0] accdst,
  output jump,
  output branch,
  output accwrite,
  output memread,
  output memwrite
);

  wire comparator_1_eq;

  Comparator #(.width(4), .mode("unsigned")) comparator_1 (.a(op), .b(4'b1111), .eq(comparator_1_eq));  // open: gt, lt
  Transistor #(.width(3)) transistor_1 (.in(op[3:1]), .out(aluop), .gate(op[0]));

  assign accdst = 2'b00;
  assign accwrite = op[0];
  assign branch = op[0];
  assign jump = op[0];
  assign memread = op[0];
  assign memwrite = op[0];
endmodule

module clock (
  input  clock,
  output pcclk,
  output opramclk,
  output memclk,
  output aluclk,
  output accclk,
  output clkout
);


  assign accclk = clock;
  assign aluclk = clock;
  assign clkout = clock;
  assign memclk = clock;
  assign opramclk = clock;
  assign pcclk = clock;
endmodule
